# Fritzing sketch Wiring (saved by Fritzing 0.9.2b)
breadboards: 1

parts:
  Composant1 = Arduino Uno (Rev3)
  R1 = Resistor [tolerance=±5% resistance=10k package="0402 [SMD]"]
  R2 = Photocell (LDR) [package=THT]

nets:
  N1: Composant1.A0, R1.Pin_0, R2.pin_1
  N2: Composant1.5V, R2.pin_0
  N3: Composant1.GND, R1.Pin_1
